// Logisim project CS240Shahriar_Mubasshir Al.circ as structural Verilog
module _3BitMultiplier (
  input  in_1,
  input  in_2,
  input  in_3,
  input  in_4,
  input  in_5,
  input  in_6,
  output out_7,
  output out_8,
  output out_9,
  output out_10,
  output out_11,
  output out_12
);

  wire and_1_out, and_2_out, and_3_out, and_4_out, and_5_out, and_6_out, and_7_out, and_8_out, and_9_out,
       n5bitadder_1_out_12, n5bitadder_1_out_13, n5bitadder_1_out_14, n5bitadder_1_out_15,
       n5bitadder_1_out_16;

  and and_1 (and_1_out, in_1, in_4);
  and and_2 (and_2_out, in_1, in_5);
  and and_3 (and_3_out, in_4, in_2);
  and and_4 (and_4_out, in_1, in_6);
  and and_5 (and_5_out, in_2, in_5);
  and and_6 (and_6_out, in_4, in_3);
  and and_7 (and_7_out, in_3, in_5);
  and and_8 (and_8_out, in_2, in_6);
  _5BitAdder u_5bitadder_1 (
    .in_1(1'b0), .in_2(and_2_out), .in_3(and_5_out), .in_4(and_7_out), .in_5(1'b0), .in_6(1'b0), .in_7(1'b0),
    .in_8(and_4_out), .in_9(and_8_out), .in_10(and_9_out), .out_12(n5bitadder_1_out_12),
    .out_13(n5bitadder_1_out_13), .out_14(n5bitadder_1_out_14), .out_15(n5bitadder_1_out_15),
    .out_16(n5bitadder_1_out_16));  // open: out_11
  _5BitAdder u_5bitadder_2 (
    .out_11(out_7), .in_1(and_1_out), .in_2(and_3_out), .in_3(and_6_out), .in_4(1'b0), .in_5(1'b0),
    .in_6(n5bitadder_1_out_12), .in_7(n5bitadder_1_out_13), .in_8(n5bitadder_1_out_14),
    .in_9(n5bitadder_1_out_15), .in_10(n5bitadder_1_out_16), .out_12(out_8), .out_13(out_9), .out_14(out_10),
    .out_15(out_11), .out_16(out_12));
  and and_9 (and_9_out, in_3, in_6);
endmodule

// FA
module FullAdder (
  input  in_1,
  input  in_2,
  input  in_3,
  output out_4,
  output out_5
);

  wire and_1_out, and_2_out, xor_1_out;

  xor xor_1 (xor_1_out, in_1, in_2);
  and and_1 (and_1_out, xor_1_out, in_3);
  and and_2 (and_2_out, in_1, in_2);
  xor xor_2 (out_4, xor_1_out, in_3);
  or or_1 (out_5, and_1_out, and_2_out);
endmodule

// HA
module HalfAdder (
  input  in_1,
  input  in_2,
  output out_3,
  output out_4
);

  xor xor_1 (out_3, in_1, in_2);
  and and_1 (out_4, in_2, in_1);
endmodule

module _5BitAdder (
  input  in_1,
  input  in_2,
  input  in_3,
  input  in_4,
  input  in_5,
  input  in_6,
  input  in_7,
  input  in_8,
  input  in_9,
  input  in_10,
  output out_11,
  output out_12,
  output out_13,
  output out_14,
  output out_15,
  output out_16
);

  wire fulladder_2_out_5, fulladder_3_out_5, fulladder_4_out_5, halfadder_1_out_4;

  FullAdder fulladder_1 (.in_1(fulladder_2_out_5), .in_2(in_1), .in_3(in_6), .out_4(out_12), .out_5(out_11));
  FullAdder fulladder_2 (.in_1(fulladder_3_out_5), .in_2(in_2), .in_3(in_7), .out_4(out_13), .out_5(fulladder_2_out_5));
  FullAdder fulladder_3 (.in_1(fulladder_4_out_5), .in_2(in_3), .in_3(in_8), .out_4(out_14), .out_5(fulladder_3_out_5));
  FullAdder fulladder_4 (.in_1(halfadder_1_out_4), .in_2(in_4), .in_3(in_9), .out_4(out_15), .out_5(fulladder_4_out_5));
  HalfAdder halfadder_1 (.in_1(in_10), .in_2(in_5), .out_3(out_16), .out_4(halfadder_1_out_4));
endmodule
